// Digital circuit CE_M_MAIN.dig as structural Verilog
module CE_M_MAIN (
  input  C,
  output [7:0] OUT,
  output C_OUT,
  output WR_OUT
);

  wire and_1_out, and_2_out, and_3_out, and_4_out, and_5_out, and_6_out, and_7_out, ce_m_cpu_1_vba_cpu,
       ce_m_cpu_1_vda_cpu, ce_m_cpu_1_vsa_cpu, ce_m_cpu_1_vva_cpu, comparator_1_eq, counter_2_ovf, nCLK,
       not_1_out, not_4_out, RD, WR;
  wire [7:0] ce_buffer_1_q, ce_buffer_2_q, ce_buffer_3_q, DI, DO, PRG_d, RAM_d;
  wire [15:0] ADDR;
  wire [15:1] counter_1_out;

  Counter #(.Bits(16)) counter_1 (.en(1'b1), .C(C), .clr(1'b0), .out({counter_1_out, C_OUT}));  // open: ovf
  and and_1 (and_1_out, not_1_out, C_OUT);
  Counter #(.Bits(2)) counter_2 (.en(1'b1), .C(and_1_out), .clr(1'b0), .ovf(counter_2_ovf));  // open: out
  not not_1 (not_1_out, counter_2_ovf);
  not not_2 (nCLK, C_OUT);
  CE_M_CPU ce_m_cpu_1 (
    .R_CPU(not_1_out), .C_CPU(C_OUT), .DI_CPU(DI), .nIRQ_CPU(1'b1), .nNMI_CPU(1'b1), .nABT_CPU(1'b1),
    .nSOB_CPU(1'b1), .nRDY_CPU(1'b1), .BE_CPU(1'b1), .DO_CPU(DO), .AO_CPU(ADDR), .RnW_CPU(RD),
    .VDA_CPU(ce_m_cpu_1_vda_cpu), .VPA_CPU(WR_OUT), .VBA_CPU(ce_m_cpu_1_vba_cpu),
    .VSA_CPU(ce_m_cpu_1_vsa_cpu), .VVA_CPU(ce_m_cpu_1_vva_cpu));  // open: nMLB_CPU
  not not_3 (WR, RD);
  Comparator #(.Bits(16)) comparator_1 (.a(ADDR), .b(16'hdf00), .eq(comparator_1_eq));  // open: gt, lt
  // Probe on ADDR
  // Probe on DO
  // Probe on DI
  and and_2 (and_2_out, ADDR[10], ADDR[11], ADDR[12], ADDR[13], ADDR[14], ADDR[15], RD);
  and and_3 (and_3_out, WR, ~comparator_1_eq);  // And
  and and_4 (and_4_out, comparator_1_eq, WR);
  not not_4 (not_4_out, comparator_1_eq);
  BlockRAMDualPort #(.AddrBits(9), .Bits(8)) RAM (.A(ADDR[8:0]), .Din(DO), .str(and_3_out), .C(C_OUT), .D(RAM_d));
  ROM #(.AddrBits(10), .Bits(8)) PRG (.A(ADDR[9:0]), .sel(1'b1), .D(PRG_d));
  and and_5 (and_5_out, RD, comparator_1_eq);
  and and_6 (and_6_out, ~and_2_out, not_4_out);  // And
  and and_7 (and_7_out, not_4_out, and_2_out);
  Register #(.Bits(8)) OUTP (.D(DO), .C(C_OUT), .en(and_4_out), .Q(OUT));
  CE_BUFFER ce_buffer_1 (.I(RAM_d), .E(and_6_out), .Q(ce_buffer_1_q));
  assign DI = ce_buffer_1_q | ce_buffer_2_q | ce_buffer_3_q;  // Or or_1, 8 bits wide
  CE_BUFFER ce_buffer_2 (.I(PRG_d), .E(and_7_out), .Q(ce_buffer_2_q));
  CE_BUFFER ce_buffer_3 (.I(OUT), .E(and_5_out), .Q(ce_buffer_3_q));

  // Other names for the same wires on the sheet: CLK = C_OUT

  // Notes on the sheet:
  //   C: Hz: 1000
  //   contents of PRG (hex, n*v repeats v):
  //   ea,40,ea,40,ea,40,a2,ff,9a,20,11,fc,ee,0,df,80,f8,38,5c,ee,0,0,5c,ee,1,0,b0,2,80,
  //   f3,60,0,0,0,0,0,0,0,0,0,0,0,0,0,0,0,0,0,0,0,0,0,0,0,0,0,0,0,0,0,0,0,0,0,0,0,0,0,0,
  //   0,0,0,0,0,0,0,0,0,0,0,0,0,0,0,0,0,0,0,0,0,0,0,0,0,0,0,0,0,0,0,0,0,0,0,0,0,0,0,0,0,
  //   0,0,0,0,0,0,0,0,0,0,0,0,0,0,0,0,0,0,0,0,0,0,0,0,0,0,0,0,0,0,0,0,0,0,0,0,0,0,0,0,0,
  //   0,0,0,0,0,0,0,0,0,0,0,0,0,0,0,0,0,0,0,0,0,0,0,0,0,0,0,0,0,0,0,0,0,0,0,0,0,0,0,0,0,
  //   0,0,0,0,0,0,0,0,0,0,0,0,0,0,0,0,0,0,0,0,0,0,0,0,0,0,0,0,0,0,0,0,0,0,0,0,0,0,0,0,0,
  //   0,0,0,0,0,0,0,0,0,0,0,0,0,0,0,0,0,0,0,0,0,0,0,0,0,0,0,0,0,0,0,0,0,0,0,0,0,0,0,0,0,
  //   0,0,0,0,0,0,0,0,0,0,0,0,0,0,0,0,0,0,0,0,0,0,0,0,0,0,0,0,0,0,0,0,0,0,0,0,0,0,0,0,0,
  //   0,0,0,0,0,0,0,0,0,0,0,0,0,0,0,0,0,0,0,0,0,0,0,0,0,0,0,0,0,0,0,0,0,0,0,0,0,0,0,0,0,
  //   0,0,0,0,0,0,0,0,0,0,0,0,0,0,0,0,0,0,0,0,0,0,0,0,0,0,0,0,0,0,0,0,0,0,0,0,0,0,0,0,0,
  //   0,0,0,0,0,0,0,0,0,0,0,0,0,0,0,0,0,0,0,0,0,0,0,0,0,0,0,0,0,0,0,0,0,0,0,0,0,0,0,0,0,
  //   0,0,0,0,0,0,0,0,0,0,0,0,0,0,0,0,0,0,0,0,0,0,0,0,0,0,0,0,0,0,0,0,0,0,0,0,0,0,0,0,0,
  //   0,0,0,0,0,0,0,0,0,0,0,0,0,0,0,0,0,0,0,0,0,0,0,0,0,0,0,0,0,0,0,0,0,0,0,0,0,0,0,0,0,
  //   0,0,0,0,0,0,0,0,0,0,0,0,0,0,0,0,0,0,0,0,0,0,0,0,0,0,0,0,0,0,0,0,0,0,0,0,0,0,0,0,0,
  //   0,0,0,0,0,0,0,0,0,0,0,0,0,0,0,0,0,0,0,0,0,0,0,0,0,0,0,0,0,0,0,0,0,0,0,0,0,0,0,0,0,
  //   0,0,0,0,0,0,0,0,0,0,0,0,0,0,0,0,0,0,0,0,0,0,0,0,0,0,0,0,0,0,0,0,0,0,0,0,0,0,0,0,0,
  //   0,0,0,0,0,0,0,0,0,0,0,0,0,0,0,0,0,0,0,0,0,0,0,0,0,0,0,0,0,0,0,0,0,0,0,0,0,0,0,0,0,
  //   0,0,0,0,0,0,0,0,0,0,0,0,0,0,0,0,0,0,0,0,0,0,0,0,0,0,0,0,0,0,0,0,0,0,0,0,0,0,0,0,0,
  //   0,0,0,0,0,0,0,0,0,0,0,0,0,0,0,0,0,0,0,0,0,0,0,0,0,0,0,0,0,0,0,0,0,0,0,0,0,0,0,0,0,
  //   0,0,0,0,0,0,0,0,0,0,0,0,0,0,0,0,0,0,0,0,0,0,0,0,0,0,0,0,0,0,0,0,0,0,0,0,0,0,0,0,0,
  //   0,0,0,0,0,0,0,0,0,0,0,0,0,0,0,0,0,0,0,0,0,0,0,0,0,0,0,0,0,0,0,0,0,0,0,0,0,0,0,0,0,
  //   0,0,0,0,0,0,0,0,0,0,0,0,0,0,0,0,0,0,0,0,0,0,0,0,0,0,0,0,0,0,0,0,0,0,0,0,0,0,0,0,0,
  //   0,0,0,0,0,0,0,0,0,0,0,0,0,0,0,0,0,0,0,0,0,0,0,0,0,0,0,0,0,0,0,0,0,0,0,0,0,0,0,0,0,
  //   0,0,0,0,0,0,0,0,0,0,0,0,0,0,0,0,0,0,0,0,0,0,0,0,0,0,0,0,0,0,0,0,0,0,0,0,0,0,0,0,0,
  //   0,0,0,0,0,0,0,0,0,0,0,0,0,0,0,0,0,0,0,0,0,0,0,0,0,0,0,0,0,0,0,0,0,0,0,0,0,0,0,0,0,
  //   0,0,0,0,4,fc,2,fc,9,fc,0,fc
endmodule
